// Logisim project Encryptor_processor.circ as structural Verilog: 1 circuit, main circuit main
module main (
  input  [7:0] in_1,
  input  start,
  input  reset,
  output busy,
  output done
);

  wire and_1_out, clock_out, not_1_out, not_2_out;
  wire [7:0] counter_1_q, ram_1_data, rom_1_data, xor_1_out;

  Clock clock (.out(clock_out));
  not not_1 (not_1_out, done);
  and and_1 (and_1_out, clock_out, not_1_out);
  Counter counter_1 (.Q(counter_1_q), .clk(and_1_out), .clr(reset));  // open: load, D, count, carry
  not not_2 (not_2_out, done);
  Comparator comparator_1 (.a(counter_1_q), .b({8{1'b1}}), .eq(done));  // open: gt, lt
  ROM rom_1 (.addr(counter_1_q), .data(rom_1_data));  // open: sel
  and u_busy (busy, start, not_2_out);
  assign xor_1_out = in_1 ^ rom_1_data;  // XOR_Gate xor_1, 8 bits wide
  RAM #(.bus("separate")) ram_1 (
    .addr(counter_1_q), .din(xor_1_out), .data(ram_1_data), .sel(1'b1), .clk(and_1_out), .ld(busy));  // open: str, clr

  // Notes on the sheet:
  //   contents of rom_1 (hex, n*v repeats v):
  //   68 65 6c 6c 6f 20 6d 79 20 6e 61 6d 65 20 69 73 20 4d 75 68 61 6d 6d 61 64 20 6b 61 68 61 66 20 73
  //   68 61 69 6b 68 2e 20 6c 65 74 73 20 74 72 79 20 74 6f 20 65 6e 63 6f 64 65 20 74 68 69 73 d a 68 65
  //   6c 6c 6f
endmodule
